// Logisim project mode3.circ as structural Verilog: 2 circuits, main circuit main
module multiplier (
  input  [7:0] A,
  input  [7:0] B,
  output [15:0] P
);

  wire inv_gate_62, inv_gate_63, inv_gate_68, inv_gate_69, inv_gate_72, inv_gate_73, inv_gate_78,
       inv_gate_79, inv_gate_104, inv_gate_105, inv_gate_192, inv_gate_193, net_34, net_35, net_36, net_37,
       net_38, net_39, net_40, net_41, net_42, net_43, net_44, net_45, net_46, net_47, net_48, net_49,
       net_50, net_51, net_52, net_53, net_54, net_55, net_56, net_57, net_58, net_59, net_60, net_61,
       net_62, net_63, net_64, net_65, net_66, net_67, net_68, net_69, net_70, net_71, net_72, net_73,
       net_74, net_75, net_76, net_77, net_78, net_79, net_80, net_81, net_82, net_83, net_84, net_85,
       net_86, net_87, net_88, net_89, net_90, net_91, net_92, net_93, net_94, net_95, net_96, net_97,
       net_98, net_99, net_100, net_101, net_102, net_103, net_104, net_105, net_106, net_107, net_108,
       net_109, net_110, net_111, net_112, net_113, net_114, net_115, net_116, net_117, net_118, net_119,
       net_120, net_121, net_122, net_123, net_124, net_125, net_126, net_127, net_128, net_129, net_130,
       net_131, net_132, net_133, net_134, net_135, net_136, net_137, net_138, net_139, net_140, net_141,
       net_142, net_143, net_144, net_145, net_146, net_147, net_148, net_149, net_150, net_151, net_152,
       net_153, net_154, net_155, net_156, net_157, net_158, net_159, net_160, net_161, net_162, net_163,
       net_164, net_165, net_166, net_167, net_168, net_169, net_170, net_171, net_172, net_173, net_174,
       net_175, net_176, net_177, net_178, net_179, net_180, net_181, net_182, net_183, net_184, net_185,
       net_186, net_187, net_188, net_189, net_190, net_191, net_192, net_193, net_194, net_195, net_196,
       net_197, net_198, net_199, net_200, net_201, net_202, net_203, net_204, net_205, net_206, net_207,
       net_208, net_209, net_210, net_211, net_212, net_213, net_214, net_215, net_216, net_217, net_218,
       net_219, net_220, net_221, net_222, net_223, net_224, net_225, net_226, net_227, net_228, net_229,
       net_230, net_231, net_232, net_233, net_234, net_235, net_236, net_237, net_238, net_239, net_240,
       net_241, net_242, net_243, net_244, net_245, net_246, net_247, net_248, net_249, net_250, net_251,
       net_252, net_253, net_254, net_255, net_256, net_257, net_258, net_259, net_260, net_261, net_262,
       net_263, net_264, net_265, net_266, net_267, net_268, net_269, net_270, net_271, net_272, net_273,
       net_274, net_275, net_276, net_277, net_278, net_279;

  not not_1 (net_34, B[4]);
  and and_1 (net_42, B[2], A[5]);
  // NAND_Gate nand_1 has open pins: out=net_50
  // NAND_Gate nand_2 has open pins: out=net_58
  // NAND_Gate nand_3 has open pins: out=net_66
  // NAND_Gate nand_4 has open pins: out=net_74
  // XNOR_Gate xnor_1 has open pins: out=net_82
  // NAND_Gate nand_5 has open pins: out=net_90
  // XNOR_Gate xnor_2 has open pins: out=net_98
  and and_2 (net_106, net_70, inv_gate_72);
  not not_2 (inv_gate_72, net_80);
  // NAND_Gate nand_6 has open pins: out=net_114
  or or_1 (net_122, net_119, net_120);
  // NAND_Gate nand_7 has open pins: out=net_130
  and and_3 (net_138, net_135, inv_gate_104);
  not not_3 (inv_gate_104, net_137);
  // XNOR_Gate xnor_3 has open pins: out=net_146
  // NAND_Gate nand_8 has open pins: out=net_154
  // NAND_Gate nand_9 has open pins: out=net_162
  // NAND_Gate nand_10 has open pins: out=net_168
  or or_2 (net_176, net_172, net_174);
  and and_4 (net_184, A[6], B[6]);
  and and_5 (net_192, net_181, net_191);
  // NAND_Gate nand_11 has open pins: out=net_200
  and and_6 (net_208, net_197, net_207);
  and and_7 (net_216, net_211, net_215);
  or or_3 (net_224, net_221, inv_gate_192);
  not not_4 (inv_gate_192, net_223);
  // NAND_Gate nand_12 has open pins: out=P[1]
  // NAND_Gate nand_13 has open pins: out=net_236
  and and_8 (P[14], net_240, net_242);
  and and_9 (net_250, net_245, net_249);
  // NAND_Gate nand_14 has open pins: out=P[3]
  and and_10 (net_263, net_46, net_262);
  and and_11 (net_270, net_268, net_269);
  // NAND_Gate nand_15 has open pins: out=P[5]
  not not_5 (inv_gate_73, net_106);
  not not_6 (inv_gate_105, net_137);
  not not_7 (inv_gate_193, net_221);
  not not_8 (net_35, B[3]);
  // NAND_Gate nand_16 has open pins: out=net_43
  // XOR_Gate xor_1 has open pins: out=net_51
  // XOR_Gate xor_2 has open pins: out=net_59
  or or_4 (net_67, net_38, net_52);
  or or_5 (net_75, net_35, net_48);
  // XNOR_Gate xnor_4 has open pins: out=net_83
  and and_12 (net_91, net_86, net_90);
  and and_13 (net_99, A[3], B[6]);
  and and_14 (net_107, net_71, inv_gate_73);
  or or_6 (net_115, net_111, net_113);
  and and_15 (net_123, net_121, net_122);
  // NAND_Gate nand_17 has open pins: out=net_131
  or or_7 (net_139, net_135, inv_gate_105);
  // NAND_Gate nand_18 has open pins: out=net_147
  // NAND_Gate nand_19 has open pins: out=net_155
  // XNOR_Gate xnor_5 has open pins: out=net_163
  // NAND_Gate nand_20 has open pins: out=net_169
  and and_16 (net_177, net_175, net_176);
  // NAND_Gate nand_21 has open pins: out=net_185
  or or_8 (net_193, net_138, net_163);
  // NAND_Gate nand_22 has open pins: out=net_201
  // NAND_Gate nand_23 has open pins: out=net_209
  // NAND_Gate nand_24 has open pins: out=net_217
  or or_9 (net_225, net_223, inv_gate_193);
  // NAND_Gate nand_25 has open pins: out=net_230
  // NAND_Gate nand_26 has open pins: out=net_237
  // NAND_Gate nand_27 has open pins: out=net_243
  // NAND_Gate nand_28 has open pins: out=P[4]
  and and_17 (P[0], A[0], B[0]);
  // NAND_Gate nand_29 has open pins: out=net_264
  // NAND_Gate nand_30 has open pins: out=net_271
  // NAND_Gate nand_31 has open pins: out=net_278
  not not_9 (net_36, B[7]);
  and and_18 (net_44, A[7], B[0]);
  // NAND_Gate nand_32 has open pins: out=net_52
  and and_19 (net_60, net_39, net_59);
  and and_20 (net_68, net_66, net_67);
  // NAND_Gate nand_33 has open pins: out=net_76
  // NAND_Gate nand_34 has open pins: out=net_84
  // NAND_Gate nand_35 has open pins: out=net_92
  // NAND_Gate nand_36 has open pins: out=net_100
  or or_10 (net_108, net_105, net_107);
  // NAND_Gate nand_37 has open pins: out=net_116
  // XNOR_Gate xnor_6 has open pins: out=net_124
  // NAND_Gate nand_38 has open pins: out=net_132
  // XNOR_Gate xnor_7 has open pins: out=net_140
  // NAND_Gate nand_39 has open pins: out=net_148
  and and_21 (net_156, net_122, net_155);
  // XNOR_Gate xnor_8 has open pins: out=net_164
  or or_11 (net_170, net_166, net_168);
  // XNOR_Gate xnor_9 has open pins: out=net_178
  // NAND_Gate nand_40 has open pins: out=net_186
  and and_22 (net_194, net_139, net_193);
  or or_12 (net_202, net_199, net_200);
  and and_23 (net_210, net_201, net_209);
  or or_13 (net_218, net_192, net_216);
  and and_24 (net_226, net_224, net_225);
  // NAND_Gate nand_41 has open pins: out=net_231
  and and_25 (net_238, net_225, net_237);
  // NAND_Gate nand_42 has open pins: out=net_244
  // NAND_Gate nand_43 has open pins: out=net_251
  // NAND_Gate nand_44 has open pins: out=net_257
  // NAND_Gate nand_45 has open pins: out=net_265
  // NAND_Gate nand_46 has open pins: out=net_272
  // XNOR_Gate xnor_10 has open pins: out=P[12]
  not not_10 (net_37, B[6]);
  and and_26 (net_45, A[7], B[1]);
  // XOR_Gate xor_3 has open pins: out=net_53
  // NAND_Gate nand_47 has open pins: out=net_61
  // NAND_Gate nand_48 has open pins: out=net_69
  // NAND_Gate nand_49 has open pins: out=net_77
  // NAND_Gate nand_50 has open pins: out=net_85
  and and_27 (net_93, A[2], B[7]);
  // NAND_Gate nand_51 has open pins: out=net_101
  // NAND_Gate nand_52 has open pins: out=net_109
  and and_28 (net_117, A[7], B[2]);
  // XNOR_Gate xnor_11 has open pins: out=net_125
  or or_14 (net_133, net_129, net_131);
  and and_29 (net_141, A[4], B[6]);
  // NAND_Gate nand_53 has open pins: out=net_149
  // NAND_Gate nand_54 has open pins: out=net_157
  // XNOR_Gate xnor_12 has open pins: out=P[10]
  and and_30 (net_171, A[7], B[4]);
  // NAND_Gate nand_55 has open pins: out=net_179
  // NAND_Gate nand_56 has open pins: out=net_187
  // NAND_Gate nand_57 has open pins: out=net_195
  // NAND_Gate nand_58 has open pins: out=net_203
  // NAND_Gate nand_59 has open pins: out=net_211
  and and_31 (net_219, net_217, net_218);
  // XNOR_Gate xnor_13 has open pins: out=net_227
  // NAND_Gate nand_60 has open pins: out=net_232
  and and_32 (net_239, net_236, net_238);
  // NAND_Gate nand_61 has open pins: out=net_245
  // NAND_Gate nand_62 has open pins: out=net_252
  // NAND_Gate nand_63 has open pins: out=net_258
  and and_33 (net_266, net_264, net_265);
  and and_34 (net_273, net_271, net_272);
  // XOR_Gate xor_4 has open pins: out=P[7]
  not not_11 (net_38, B[5]);
  // NAND_Gate nand_64 has open pins: out=net_46
  and and_35 (net_54, A[2], B[5]);
  // NAND_Gate nand_65 has open pins: out=net_62
  // NAND_Gate nand_66 has open pins: out=net_70
  // NAND_Gate nand_67 has open pins: out=net_78
  or or_15 (net_86, net_36, net_58);
  // NAND_Gate nand_68 has open pins: out=net_94
  or or_16 (net_102, net_99, inv_gate_68);
  not not_12 (inv_gate_68, net_101);
  // XOR_Gate xor_5 has open pins: out=net_110
  // NAND_Gate nand_69 has open pins: out=net_118
  // XNOR_Gate xnor_14 has open pins: out=net_126
  // NAND_Gate nand_70 has open pins: out=net_134
  // NAND_Gate nand_71 has open pins: out=net_142
  // NAND_Gate nand_72 has open pins: out=net_150
  or or_17 (net_158, net_154, net_156);
  // XOR_Gate xor_6 has open pins: out=P[8]
  and and_36 (net_172, A[6], B[5]);
  and and_37 (net_180, net_169, net_179);
  or or_18 (net_188, net_184, net_186);
  and and_38 (net_196, net_133, net_195);
  // NAND_Gate nand_73 has open pins: out=net_204
  or or_19 (net_212, net_208, net_210);
  and and_39 (net_220, A[7], B[6]);
  // XNOR_Gate xnor_15 has open pins: out=P[13]
  and and_40 (net_233, net_231, net_232);
  // NAND_Gate nand_74 has open pins: out=net_240
  // NAND_Gate nand_75 has open pins: out=net_246
  and and_41 (net_253, net_251, net_252);
  // NAND_Gate nand_76 has open pins: out=net_259
  and and_42 (net_267, net_263, net_266);
  // NAND_Gate nand_77 has open pins: out=net_274
  and and_43 (net_279, net_197, net_198);
  not not_13 (inv_gate_69, net_99);
  and and_44 (net_39, A[0], B[7]);
  // XNOR_Gate xnor_16 has open pins: out=net_47
  // NAND_Gate nand_78 has open pins: out=net_55
  or or_20 (net_63, net_37, net_55);
  or or_21 (net_71, net_34, net_50);
  // XNOR_Gate xnor_17 has open pins: out=net_79
  // NAND_Gate nand_79 has open pins: out=net_87
  and and_45 (net_95, net_63, net_94);
  or or_22 (net_103, net_101, inv_gate_69);
  // NAND_Gate nand_80 has open pins: out=net_111
  // NAND_Gate nand_81 has open pins: out=net_119
  // XNOR_Gate xnor_18 has open pins: out=net_127
  // NAND_Gate nand_82 has open pins: out=net_135
  and and_46 (net_143, net_109, net_142);
  or or_23 (net_151, net_147, net_149);
  and and_47 (net_159, net_157, net_158);
  and and_48 (net_165, A[5], B[7]);
  // NAND_Gate nand_83 has open pins: out=net_173
  // NAND_Gate nand_84 has open pins: out=net_181
  // NAND_Gate nand_85 has open pins: out=net_189
  // NAND_Gate nand_86 has open pins: out=net_197
  // XNOR_Gate xnor_19 has open pins: out=net_205
  and and_49 (net_213, net_181, net_182);
  and and_50 (net_221, A[6], B[7]);
  // XOR_Gate xor_7 has open pins: out=P[9]
  // NAND_Gate nand_87 has open pins: out=P[2]
  or or_24 (net_241, net_236, net_238);
  // NAND_Gate nand_88 has open pins: out=net_247
  // NAND_Gate nand_89 has open pins: out=net_254
  and and_51 (net_260, net_258, net_259);
  // NAND_Gate nand_90 has open pins: out=P[6]
  // NAND_Gate nand_91 has open pins: out=net_275
  // XNOR_Gate xnor_20 has open pins: out=P[11]
  not not_14 (inv_gate_62, net_95);
  not not_15 (inv_gate_78, net_79);
  and and_52 (net_40, A[3], B[4]);
  // NAND_Gate nand_92 has open pins: out=net_48
  // XOR_Gate xor_8 has open pins: out=net_56
  // NAND_Gate nand_93 has open pins: out=net_64
  // NAND_Gate nand_94 has open pins: out=net_72
  // XNOR_Gate xnor_21 has open pins: out=net_80
  // XNOR_Gate xnor_22 has open pins: out=net_88
  or or_25 (net_96, net_93, inv_gate_62);
  // XNOR_Gate xnor_23 has open pins: out=net_104
  and and_53 (net_112, net_74, inv_gate_78);
  // NAND_Gate nand_95 has open pins: out=net_120
  // XNOR_Gate xnor_24 has open pins: out=net_128
  // NAND_Gate nand_96 has open pins: out=net_136
  or or_26 (net_144, net_141, net_143);
  // NAND_Gate nand_97 has open pins: out=net_152
  // XNOR_Gate xnor_25 has open pins: out=net_160
  // NAND_Gate nand_98 has open pins: out=net_166
  // NAND_Gate nand_99 has open pins: out=net_174
  or or_27 (net_182, net_165, net_180);
  // XNOR_Gate xnor_26 has open pins: out=net_190
  or or_28 (net_198, net_194, net_196);
  // XNOR_Gate xnor_27 has open pins: out=net_206
  // XOR_Gate xor_9 has open pins: out=net_214
  // NAND_Gate nand_100 has open pins: out=net_222
  // NAND_Gate nand_101 has open pins: out=net_228
  // NAND_Gate nand_102 has open pins: out=net_234
  // NOR_Gate nor_1 has open pins: out=P[15]
  and and_54 (net_248, net_243, net_246);
  // NAND_Gate nand_103 has open pins: out=net_255
  and and_55 (net_261, net_257, net_260);
  // NAND_Gate nand_104 has open pins: out=net_268
  and and_56 (net_276, net_274, net_275);
  not not_16 (inv_gate_63, net_93);
  not not_17 (inv_gate_79, net_112);
  and and_57 (net_41, B[3], A[4]);
  // XOR_Gate xor_10 has open pins: out=net_49
  and and_58 (net_57, A[1], B[6]);
  // NAND_Gate nand_105 has open pins: out=net_65
  // NAND_Gate nand_106 has open pins: out=net_73
  // XNOR_Gate xnor_28 has open pins: out=net_81
  // NAND_Gate nand_107 has open pins: out=net_89
  or or_29 (net_97, net_95, inv_gate_63);
  // NAND_Gate nand_108 has open pins: out=net_105
  and and_59 (net_113, net_75, inv_gate_79);
  // NAND_Gate nand_109 has open pins: out=net_121
  // NAND_Gate nand_110 has open pins: out=net_129
  // NAND_Gate nand_111 has open pins: out=net_137
  // NAND_Gate nand_112 has open pins: out=net_145
  and and_60 (net_153, A[7], B[3]);
  // XNOR_Gate xnor_29 has open pins: out=net_161
  // NAND_Gate nand_113 has open pins: out=net_167
  // NAND_Gate nand_114 has open pins: out=net_175
  and and_61 (net_183, A[7], B[5]);
  // NAND_Gate nand_115 has open pins: out=net_191
  // NAND_Gate nand_116 has open pins: out=net_199
  // NAND_Gate nand_117 has open pins: out=net_207
  // NAND_Gate nand_118 has open pins: out=net_215
  and and_62 (net_223, net_187, net_222);
  // NAND_Gate nand_119 has open pins: out=net_229
  // NAND_Gate nand_120 has open pins: out=net_235
  // NAND_Gate nand_121 has open pins: out=net_242
  and and_63 (net_249, net_244, net_247);
  and and_64 (net_256, net_254, net_255);
  // NAND_Gate nand_122 has open pins: out=net_262
  // NAND_Gate nand_123 has open pins: out=net_269
  and and_65 (net_277, net_273, net_276);

  // Other names for the same wires on the sheet: net_2 = A[0]; net_3 = A[1]; net_4 = A[2]; net_5 = A[3]; net_6 = A[4];
  //   net_7 = A[5]; net_8 = A[6]; net_9 = A[7]; net_10 = B[0]; net_11 = B[1]; net_12 = B[2]; net_13 = B[3];
  //   net_14 = B[4]; net_15 = B[5]; net_16 = B[6]; net_17 = B[7]; net_18 = P[0]; net_19 = P[1]; net_20 = P[2];
  //   net_21 = P[3]; net_22 = P[4]; net_23 = P[5]; net_24 = P[6]; net_25 = P[7]; net_26 = P[8]; net_27 = P[9];
  //   net_28 = P[10]; net_29 = P[11]; net_30 = P[12]; net_31 = P[13]; net_32 = P[14]; net_33 = P[15]
endmodule

module main (
  input  [7:0] A,
  input  [7:0] B,
  output [15:0] P
);


  // Other names for the same wires on the sheet: main_A[7:0] = A; main_B[7:0] = B; main_P[15:0] = P
endmodule
